# Fritzing sketch Robotics101 (saved by Fritzing 1.0.1rc)
breadboards: 1

parts:
  L298N1 = L298N DC motor driver
  A1 = Esp32-c3 super mini
  VCC3 = Battery block 9V
  M1 = DC Mini Metal Gear Motor
  M2 = DC Mini Metal Gear Motor
  U1 = SWITCH_SPDT [package=kps-1290]

nets:
  N1: L298N1.OUT1, M2.IN2
  N2: L298N1.OUT2, M2.IN1
  N3: L298N1.OUT3, M1.IN2
  N4: L298N1.OUT4, M1.IN1
  N5: L298N1.12V, U1.S
  N6: L298N1.GND, A1.Pin_15, VCC3.-
  N7: L298N1.5V#7, A1.Pin_16
  N8: L298N1.5V#9, L298N1.ENA
  N9: L298N1.5V#10, L298N1.ENB
  N10: L298N1.IN1, A1.Pin_13
  N11: L298N1.IN2, A1.Pin_12
  N12: L298N1.IN3, A1.Pin_11
  N13: L298N1.IN4, A1.Pin_10
  N14: VCC3.+, U1.P

custom parts:
  L298N DC motor driver: 2x DC motor driver with 78M05 positive voltage regulator (7..35 V) L298N: max 46 V, 2 A Set 5 V Enable jumper to enable 5 V regultor (needed for the L298N) and +5 V output at screw terminal or supply external +5 V at screw terminal Set ENA and/or ENB to +5 V to enable motor permanently or supply ENA and/or ENB with PWM signal IN1 and IN2 set rotation directory for motor A (OUT1/OUT2) IN2 and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
  Esp32-c3 super mini: ESP32-C3 Development Board ESP32 SuperMini Development Board ESP32 Development Board WiFi Bluetooth.
